# Fritzing sketch wemos_neopixel_nightlight (saved by Fritzing 0.9.3b)
circuit board: 4.5cm x 4.5cm

parts:
  Part1 = 16 NeoPixel Ring [part_number=1463]
  WeMos_D1_Mini1 = WeMos D1 Mini
  J1 = female pin header, 4 pins [form="♀ (female)"]
  R1 = Resistor [tolerance=±5% resistance=4.7k package=THT]

nets:
  N1: Part1.IN, WeMos_D1_Mini1.D0
  VDD: Part1.VDD, WeMos_D1_Mini1.5V
  N2: Part1.GND, WeMos_D1_Mini1.G, J1.pin4
  N3: WeMos_D1_Mini1.3V3, R1.Pin_1
  N4: WeMos_D1_Mini1.D5, J1.pin2
  N5: J1.pin1, R1.Pin_0

custom parts:
  16 NeoPixel Ring: 16 ultra bright smart LED NeoPixels are arranged in a circle with 1.75" (44.5mm) outer diameter. The rings are 'chainable' - connect the output pin of one to the input pin of another. Use only one microcontroller pin to control as many as you can chain together! Each LED is addressable as the driver chip is inside the LED. Each one has ~18mA constant current drive so the color will be very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
